# Fritzing sketch arduino_sensor_distance (saved by Fritzing 0.9.3b)
breadboards: 1

parts:
  Componente1 = Arduino Uno (Rev3)  # not connected
  Componente2 = Arduino Ethernet Shield (Rev3)
  hc-sr1 = hc-sr04
  J1 = Piezo Speaker
  LED1 = LED - 5mm [color="Red (633nm)" package="5 mm [THT]"]
  R1 = Resistor [tolerance=±5% resistance=220 package=THT]

nets:
  N1: Componente2.D8, LED1.anode
  N2: Componente2.PWM_D9, J1.pin2
  GND: Componente2.GND, hc-sr1.GND, J1.pin1, R1.Pin_1
  N3: Componente2.D2, hc-sr1.Trig
  N4: Componente2.PWM_D3, hc-sr1.Echo
  5V: Componente2.5V, hc-sr1.VCC
  N5: LED1.cathode, R1.Pin_0

// code stored in the sketch: Leitura_SensorDistancia.ino
/**
  Leitura de sensor
  @author Anderson Wilmer
*/


#include <SPI.h>
#include <Ethernet.h>
#include <DistanceSensor.h>


#define red 8


constexpr int TrigPin = 2;  //Pino Trig do sensor
constexpr int EchoPin = 3;  //Pino Echo do sensor
DistanceSensor<TrigPin, EchoPin> sensor;



// Gerar o MAC ADDRESS (https://ssl.crox.net/arduinomac)
byte mac[6] = { 0x90, 0xA2, 0xDA, 0x49, 0xDE, 0x76 };
EthernetServer server(80);


const char pagina[] PROGMEM = R"HTML(<!DOCTYPE html>
<html lang="pt-br">
<head>
    <meta charset="UTF-8">
    <meta name="viewport" content="width=device-width, initial-scale=1.0">
    <title>Sensor Ultrassônico</title>
    <style>
        body {
            font-family: sans-serif;
            text-align: center;
        }


        h1 {
            font-size: 1.9rem;
            color: rgb(0, 0, 0);
        }


        #alerta {
            color: #ff0000;
            font-size: 1.5rem;
            margin-top: 30px;
        }
    </style>
</head>
<body>
    <h1>Sensor Ultrassônico</h1>
    <h2>Distância</h2>
    <div id="sensor">--</div>
    <div id="alerta"></div>


    <script>
        function atualizar() {
            fetch("/json")
            .then(res => res.json())
            .then(dados => {
                let distancia = dados.distancia;


                document.getElementById("sensor").innerHTML = distancia + " cm"


                let alerta = document.getElementById("alerta") 
                if (distancia > 10 && distancia < 30) {
                    alerta.innerHTML = "ALERTA"
                } else if (distancia > 2 && distancia <= 10) {
                    alerta.innerHTML = "DANGER"
                } else {
                    alerta.innerHTML = ""
                }
            })
        }
        setInterval(atualizar, 200)
    </script>


    
</body>
</html>
)HTML";


void setup() {
  
  Serial.begin(9600);
  Ethernet.begin(mac);
  server.begin();
  Serial.println("Servidor WEB");
  Serial.print("IP do Servidor: ");
  Serial.println(Ethernet.localIP());
  pinMode(8, OUTPUT);
  pinMode(9, OUTPUT);
  //Incialização do sensor HC-SR04
  sensor.begin();
}


void loop() {
  // Uso do sensor
  int distancia = sensor.tick();  // faz a leitura do sensor
  if (distancia == sensor.NREADY) {
    return;
  }


  Serial.print("Distância: ");
  Serial.print(distancia);
  Serial.println("cm");



  if (distancia > 10 && distancia < 30) {
    digitalWrite(8, HIGH);
  } else {
    digitalWrite(8, LOW);
  }


  if (distancia > 2 && distancia <= 10) {
    digitalWrite(9, HIGH);
    digitalWrite(red, HIGH);
    tone(12, 700);
    delay(distancia * 50);
    digitalWrite(9, LOW);
    digitalWrite(red, LOW);
    delay(distancia * 50);
    noTone(12);


    //digitalWrite(12, LOW); //buzzer
  } else {
    digitalWrite(9, LOW);
    noTone(12);
    //digitalWrite(12, LOW);
  }
  EthernetClient client = server.available();


  if (client) {


    String request = "";


    while (client.available()) {
      char c = client.read();
      request += c;
    }


    // endpoint JSON
    if (request.indexOf("GET /json") >= 0) {


      client.println(F("HTTP/1.1 200 OK"));
      client.println(F("Content-Type: application/json"));
      client.println(F("Connection: close"));
      client.println();


      client.print("{\"distancia\":");
      client.print(distancia);
      client.print("}");


      delay(1);
      client.stop();
      return;
    }


    // página principal
    client.println(F("HTTP/1.1 200 OK"));
    client.println(F("Content-Type: text/html"));
    client.println(F("Connection: close"));
    client.println();


    client.print((__FlashStringHelper*)pagina);


    delay(100);


    client.stop();
  }
}
